// Digital circuit alu output to input.dig as structural Verilog
module alu_output_to_input (
  input  A1,
  input  A2,
  input  A3,
  input  A4,
  input  A5,
  input  A6,
  input  A7,
  input  A8,
  input  A_S,
  input  in_10,
  output out_11,
  output out_12,
  output out_13,
  output out_14,
  output out_15,
  output out_16,
  output out_17,
  output out_18,
  output out_19
);

  wire FA1_c_o, FA1_s, FA2_c_o, FA2_s, FA3_c_o, FA3_s, FA4_c_o, FA4_s, FA5_c_o, FA5_s, FA6_c_o, FA6_s,
       FA7_c_o, FA7_s, FA8_c_o, FA8_s, xor_1_out, xor_2_out, xor_3_out, xor_4_out, xor_5_out, xor_6_out,
       xor_7_out, xor_8_out;

  xor xor_1 (xor_1_out, out_12, A_S);
  Add FA8 (.a(A8), .b(xor_1_out), .c_i(FA7_c_o), .s(FA8_s), .c_o(FA8_c_o));
  xor xor_2 (xor_2_out, out_13, A_S);
  Add FA7 (.a(A7), .b(xor_2_out), .c_i(FA6_c_o), .s(FA7_s), .c_o(FA7_c_o));
  Add FA6 (.a(A6), .b(xor_3_out), .c_i(FA5_c_o), .s(FA6_s), .c_o(FA6_c_o));
  xor xor_3 (xor_3_out, out_14, A_S);
  xor xor_4 (xor_4_out, out_15, A_S);
  Add FA5 (.a(A5), .b(xor_4_out), .c_i(FA4_c_o), .s(FA5_s), .c_o(FA5_c_o));
  D_FF D9 (.D(FA8_c_o), .C(in_10), .Q(out_11));  // open: nQ
  Add FA4 (.a(A4), .b(xor_5_out), .c_i(FA3_c_o), .s(FA4_s), .c_o(FA4_c_o));
  D_FF D8 (.D(FA8_s), .C(in_10), .Q(out_12));  // open: nQ
  xor xor_5 (xor_5_out, out_16, A_S);
  D_FF D7 (.D(FA7_s), .C(in_10), .Q(out_13));  // open: nQ
  D_FF D6 (.D(FA6_s), .C(in_10), .Q(out_14));  // open: nQ
  xor xor_6 (xor_6_out, out_17, A_S);
  Add FA3 (.a(A3), .b(xor_6_out), .c_i(FA2_c_o), .s(FA3_s), .c_o(FA3_c_o));
  D_FF D5 (.D(FA5_s), .C(in_10), .Q(out_15));  // open: nQ
  Add FA2 (.a(A2), .b(xor_7_out), .c_i(FA1_c_o), .s(FA2_s), .c_o(FA2_c_o));
  D_FF D4 (.D(FA4_s), .C(in_10), .Q(out_16));  // open: nQ
  xor xor_7 (xor_7_out, out_18, A_S);
  D_FF D3 (.D(FA3_s), .C(in_10), .Q(out_17));  // open: nQ
  D_FF D2 (.D(FA2_s), .C(in_10), .Q(out_18));  // open: nQ
  xor xor_8 (xor_8_out, out_19, A_S);
  Add FA1 (.a(A1), .b(xor_8_out), .c_i(A_S), .s(FA1_s), .c_o(FA1_c_o));
  D_FF D1 (.D(FA1_s), .C(in_10), .Q(out_19));  // open: nQ
endmodule
