// Digital circuit 7 segment connected to RAM and ALU with Bus.dig as structural Verilog
module _7_segment_connected_to_RAM_and_ALU_with_Bus (
  input  RAM_address,
  input  RAM_address_2,
  input  feed_in_RAM,
  input  write_in_register_A,
  input  write_in_register_B,
  input  Add_Sub,
  input  in_7,
  input  in_8,
  input  in_9,
  input  in_10,
  input  Feed_in_7_Segment
);

  wire add_1_c_o, add_2_c_o, add_3_c_o, add_4_c_o, and_1_out, and_2_out, and_3_out, and_4_out, and_5_out,
       and_6_out, and_7_out, and_8_out, and_9_out, and_10_out, and_11_out, and_12_out, and_13_out,
       and_14_out, and_15_out, and_16_out, and_17_out, and_18_out, and_19_out, and_20_out, and_21_out,
       and_22_out, and_23_out, and_24_out, and_25_out, and_26_out, and_27_out, and_28_out, and_29_out,
       and_30_out, and_31_out, and_32_out, and_33_out, and_34_out, and_35_out, and_36_out, and_37_out,
       and_38_out, and_39_out, and_40_out, and_41_out, and_42_out, and_43_out, and_44_out, and_45_out,
       and_46_out, and_47_out, and_48_out, and_49_out, and_50_out, and_51_out, and_52_out, and_53_out,
       and_54_out, d_ff_1_q, d_ff_2_q, d_ff_3_q, d_ff_4_q, d_ff_5_q, d_ff_6_q, d_ff_7_q, d_ff_8_q, d_ff_9_q,
       d_ff_10_q, d_ff_11_q, d_ff_12_q, d_ff_13_q, d_ff_14_q, d_ff_15_q, d_ff_16_q, d_ff_17_q, d_ff_18_q,
       d_ff_19_q, d_ff_20_q, d_ff_21_q, d_ff_22_q, d_ff_23_q, d_ff_24_q, d_ff_25_q, d_ff_26_q, d_ff_27_q,
       d_ff_28_q, not_1_out, not_2_out, not_3_out, not_4_out, not_5_out, not_6_out, not_7_out, not_8_out,
       or_1_out, or_2_out, or_3_out, or_4_out, or_5_out, or_6_out, or_7_out, or_8_out, or_9_out, or_10_out,
       or_11_out, or_12_out, or_13_out, or_14_out, or_15_out, or_16_out, or_17_out, or_18_out, or_19_out,
       switch_1_b, switch_2_b, switch_3_b, switch_4_b, switch_9_b, switch_10_b, switch_11_b, switch_12_b,
       xor_1_out, xor_2_out, xor_3_out, xor_4_out;

  not not_1 (not_1_out, RAM_address_2);
  not not_2 (not_2_out, RAM_address);
  not not_3 (not_3_out, RAM_address);
  not not_4 (not_4_out, RAM_address_2);
  and and_1 (and_1_out, not_1_out, not_2_out);
  and and_2 (and_2_out, RAM_address_2, not_3_out);
  and and_3 (and_3_out, not_4_out, RAM_address);
  and and_4 (and_4_out, RAM_address_2, RAM_address);
  and and_5 (and_5_out, feed_in_RAM, and_1_out);
  and and_6 (and_6_out, feed_in_RAM, and_2_out);
  and and_7 (and_7_out, feed_in_RAM, and_3_out);
  and and_8 (and_8_out, feed_in_RAM, and_4_out);
  D_FF d_ff_1 (.D(switch_1_b), .C(and_5_out), .Q(d_ff_1_q));  // open: nQ
  D_FF d_ff_2 (.D(switch_1_b), .C(and_6_out), .Q(d_ff_2_q));  // open: nQ
  D_FF d_ff_3 (.D(switch_1_b), .C(and_7_out), .Q(d_ff_3_q));  // open: nQ
  D_FF d_ff_4 (.D(switch_1_b), .C(and_8_out), .Q(d_ff_4_q));  // open: nQ
  D_FF d_ff_5 (.D(switch_3_b), .C(and_5_out), .Q(d_ff_5_q));  // open: nQ
  D_FF d_ff_6 (.D(switch_2_b), .C(and_5_out), .Q(d_ff_6_q));  // open: nQ
  D_FF d_ff_7 (.D(switch_3_b), .C(and_6_out), .Q(d_ff_7_q));  // open: nQ
  D_FF d_ff_8 (.D(switch_2_b), .C(and_6_out), .Q(d_ff_8_q));  // open: nQ
  D_FF d_ff_9 (.D(switch_3_b), .C(and_7_out), .Q(d_ff_9_q));  // open: nQ
  D_FF d_ff_10 (.D(switch_2_b), .C(and_7_out), .Q(d_ff_10_q));  // open: nQ
  D_FF d_ff_11 (.D(switch_3_b), .C(and_8_out), .Q(d_ff_11_q));  // open: nQ
  D_FF d_ff_12 (.D(switch_2_b), .C(and_8_out), .Q(d_ff_12_q));  // open: nQ
  D_FF d_ff_13 (.D(switch_4_b), .C(and_5_out), .Q(d_ff_13_q));  // open: nQ
  D_FF d_ff_14 (.D(switch_4_b), .C(and_6_out), .Q(d_ff_14_q));  // open: nQ
  D_FF d_ff_15 (.D(switch_4_b), .C(and_7_out), .Q(d_ff_15_q));  // open: nQ
  D_FF d_ff_16 (.D(switch_4_b), .C(and_8_out), .Q(d_ff_16_q));  // open: nQ
  and and_9 (and_9_out, d_ff_13_q, and_1_out);
  and and_10 (and_10_out, d_ff_5_q, and_1_out);
  and and_11 (and_11_out, d_ff_6_q, and_1_out);
  and and_12 (and_12_out, d_ff_1_q, and_1_out);
  and and_13 (and_13_out, d_ff_14_q, and_2_out);
  and and_14 (and_14_out, d_ff_7_q, and_2_out);
  and and_15 (and_15_out, d_ff_8_q, and_2_out);
  and and_16 (and_16_out, d_ff_2_q, and_2_out);
  and and_17 (and_17_out, d_ff_15_q, and_3_out);
  and and_18 (and_18_out, d_ff_9_q, and_3_out);
  and and_19 (and_19_out, d_ff_10_q, and_3_out);
  and and_20 (and_20_out, d_ff_3_q, and_3_out);
  and and_21 (and_21_out, d_ff_16_q, and_4_out);
  and and_22 (and_22_out, d_ff_11_q, and_4_out);
  and and_23 (and_23_out, d_ff_12_q, and_4_out);
  and and_24 (and_24_out, d_ff_4_q, and_4_out);
  or or_1 (or_1_out, and_12_out, and_16_out);
  or or_2 (or_2_out, and_20_out, and_24_out);
  or or_3 (or_3_out, and_11_out, and_15_out);
  or or_4 (or_4_out, and_19_out, and_23_out);
  or or_5 (or_5_out, and_10_out, and_14_out);
  or or_6 (or_6_out, and_18_out, and_22_out);
  or or_7 (or_7_out, and_9_out, and_13_out);
  or or_8 (or_8_out, and_17_out, and_21_out);
  or or_9 (or_9_out, or_1_out, or_2_out);
  or or_10 (or_10_out, or_3_out, or_4_out);
  or or_11 (or_11_out, or_5_out, or_6_out);
  or or_12 (or_12_out, or_7_out, or_8_out);
  Switch switch_1 (.A(or_9_out), .B(switch_1_b));
  Switch switch_2 (.A(or_10_out), .B(switch_2_b));
  Switch switch_3 (.A(or_11_out), .B(switch_3_b));
  Switch switch_4 (.A(or_12_out), .B(switch_4_b));
  Seven_Seg seven_seg_1 (
    .a(or_13_out), .b(or_14_out), .c(or_15_out), .d(or_16_out), .e(or_17_out), .f(or_18_out), .g(or_19_out),
    .dp(1'b0));
  Switch switch_5 (.A(in_8), .B(switch_2_b));
  Switch switch_6 (.A(in_7), .B(switch_1_b));
  Switch switch_7 (.A(in_9), .B(switch_3_b));
  D_FF d_ff_17 (.D(switch_1_b), .C(Feed_in_7_Segment), .Q(d_ff_17_q));  // open: nQ
  D_FF d_ff_18 (.D(switch_2_b), .C(Feed_in_7_Segment), .Q(d_ff_18_q));  // open: nQ
  not not_5 (not_5_out, d_ff_17_q);
  Switch switch_8 (.A(in_10), .B(switch_4_b));
  D_FF d_ff_19 (.D(switch_3_b), .C(Feed_in_7_Segment), .Q(d_ff_19_q));  // open: nQ
  D_FF d_ff_20 (.D(switch_4_b), .C(Feed_in_7_Segment), .Q(d_ff_20_q));  // open: nQ
  not not_6 (not_6_out, d_ff_18_q);
  not not_7 (not_7_out, d_ff_19_q);
  not not_8 (not_8_out, d_ff_20_q);
  and and_25 (and_25_out, not_8_out, not_7_out);
  and and_26 (and_26_out, not_6_out, not_5_out);
  and and_27 (and_27_out, d_ff_20_q, not_7_out);
  and and_28 (and_28_out, not_6_out, not_5_out);
  and and_29 (and_29_out, not_8_out, d_ff_19_q);
  and and_30 (and_30_out, not_6_out, not_5_out);
  and and_31 (and_31_out, d_ff_20_q, d_ff_19_q);
  and and_32 (and_32_out, not_6_out, not_5_out);
  and and_33 (and_33_out, not_8_out, not_7_out);
  and and_34 (and_34_out, d_ff_18_q, not_5_out);
  and and_35 (and_35_out, d_ff_20_q, not_7_out);
  and and_36 (and_36_out, d_ff_18_q, not_5_out);
  and and_37 (and_37_out, not_8_out, d_ff_19_q);
  and and_38 (and_38_out, d_ff_18_q, not_5_out);
  and and_39 (and_39_out, d_ff_20_q, d_ff_19_q);
  and and_40 (and_40_out, d_ff_18_q, not_5_out);
  and and_41 (and_41_out, not_8_out, not_7_out);
  and and_42 (and_42_out, not_6_out, d_ff_17_q);
  and and_43 (and_43_out, d_ff_20_q, not_7_out);
  and and_44 (and_44_out, not_6_out, d_ff_17_q);
  Switch switch_9 (.A(switch_1_b), .B(switch_9_b));
  and and_45 (and_45_out, and_25_out, and_26_out);
  and and_46 (and_46_out, and_27_out, and_28_out);
  and and_47 (and_47_out, and_29_out, and_30_out);
  and and_48 (and_48_out, and_31_out, and_32_out);
  and and_49 (and_49_out, and_33_out, and_34_out);
  and and_50 (and_50_out, and_35_out, and_36_out);
  and and_51 (and_51_out, and_37_out, and_38_out);
  and and_52 (and_52_out, and_39_out, and_40_out);
  and and_53 (and_53_out, and_41_out, and_42_out);
  and and_54 (and_54_out, and_43_out, and_44_out);
  Switch switch_10 (.A(switch_2_b), .B(switch_10_b));
  Switch switch_11 (.A(switch_3_b), .B(switch_11_b));
  Switch switch_12 (.A(switch_4_b), .B(switch_12_b));
  D_FF d_ff_21 (.D(switch_2_b), .C(write_in_register_A), .Q(d_ff_21_q));  // open: nQ
  D_FF d_ff_22 (.D(switch_1_b), .C(write_in_register_A), .Q(d_ff_22_q));  // open: nQ
  D_FF d_ff_23 (.D(switch_3_b), .C(write_in_register_A), .Q(d_ff_23_q));  // open: nQ
  D_FF d_ff_24 (.D(switch_4_b), .C(write_in_register_A), .Q(d_ff_24_q));  // open: nQ
  or or_13 (or_13_out, and_45_out, and_47_out, and_48_out, and_50_out, and_51_out, and_52_out, and_53_out, and_54_out);
  or or_14 (or_14_out, and_45_out, and_46_out, and_47_out, and_48_out, and_49_out, and_52_out, and_53_out, and_54_out);
  or or_15 (or_15_out, and_45_out, and_46_out, and_48_out, and_49_out, and_50_out, and_51_out, and_52_out, and_53_out, and_54_out);
  or or_16 (or_16_out, and_45_out, and_47_out, and_48_out, and_50_out, and_51_out, and_53_out, and_54_out);
  or or_17 (or_17_out, and_45_out, and_47_out, and_51_out, and_53_out);
  or or_18 (or_18_out, and_45_out, and_49_out, and_50_out, and_51_out, and_53_out, and_54_out);
  or or_19 (or_19_out, and_47_out, and_48_out, and_49_out, and_50_out, and_51_out, and_53_out, and_54_out);
  Add add_1 (.a(xor_1_out), .b(d_ff_22_q), .c_i(add_2_c_o), .s(switch_9_b), .c_o(add_1_c_o));
  Add add_2 (.a(xor_2_out), .b(d_ff_21_q), .c_i(add_3_c_o), .s(switch_10_b), .c_o(add_2_c_o));
  xor xor_1 (xor_1_out, d_ff_26_q, Add_Sub);
  Add add_3 (.a(xor_3_out), .b(d_ff_23_q), .c_i(add_4_c_o), .s(switch_11_b), .c_o(add_3_c_o));
  D_FF d_ff_25 (.D(switch_2_b), .C(write_in_register_B), .Q(d_ff_25_q));  // open: nQ
  D_FF d_ff_26 (.D(switch_1_b), .C(write_in_register_B), .Q(d_ff_26_q));  // open: nQ
  xor xor_2 (xor_2_out, d_ff_25_q, Add_Sub);
  D_FF d_ff_27 (.D(switch_3_b), .C(write_in_register_B), .Q(d_ff_27_q));  // open: nQ
  xor xor_3 (xor_3_out, d_ff_27_q, Add_Sub);
  Add add_4 (.a(xor_4_out), .b(d_ff_24_q), .c_i(Add_Sub), .s(switch_12_b), .c_o(add_4_c_o));
  D_FF d_ff_28 (.D(switch_4_b), .C(write_in_register_B), .Q(d_ff_28_q));  // open: nQ
  xor xor_4 (xor_4_out, d_ff_28_q, Add_Sub);
endmodule
