// Digital circuit 7seg display.dig as structural Verilog
module _7seg_display (
  input  in_1,
  input  in_2,
  input  in_3,
  input  in_4
);

  wire and_1_out, and_2_out, and_3_out, and_4_out, and_5_out, and_6_out, and_7_out, and_8_out, and_9_out,
       and_10_out, and_11_out, and_12_out, and_13_out, and_14_out, and_15_out, and_16_out, and_17_out,
       and_18_out, and_19_out, and_20_out, and_21_out, and_22_out, and_23_out, and_24_out, and_25_out,
       and_26_out, and_27_out, and_28_out, and_29_out, and_30_out, not_1_out, not_2_out, not_3_out, not_4_out;

  not not_1 (not_1_out, in_1);
  not not_2 (not_2_out, in_2);
  not not_3 (not_3_out, in_3);
  not not_4 (not_4_out, in_4);
  and and_1 (and_1_out, not_4_out, not_3_out);
  and and_2 (and_2_out, not_2_out, not_1_out);
  and and_3 (and_3_out, in_4, not_3_out);
  and and_4 (and_4_out, not_2_out, not_1_out);
  and and_5 (and_5_out, not_4_out, in_3);
  and and_6 (and_6_out, not_2_out, not_1_out);
  and and_7 (and_7_out, in_4, in_3);
  and and_8 (and_8_out, not_2_out, not_1_out);
  and and_9 (and_9_out, not_4_out, not_3_out);
  and and_10 (and_10_out, in_2, not_1_out);
  and and_11 (and_11_out, in_4, not_3_out);
  and and_12 (and_12_out, in_2, not_1_out);
  and and_13 (and_13_out, not_4_out, in_3);
  and and_14 (and_14_out, in_2, not_1_out);
  and and_15 (and_15_out, in_4, in_3);
  and and_16 (and_16_out, in_2, not_1_out);
  and and_17 (and_17_out, not_4_out, not_3_out);
  and and_18 (and_18_out, not_2_out, in_1);
  and and_19 (and_19_out, in_4, not_3_out);
  and and_20 (and_20_out, not_2_out, in_1);
  and and_21 (and_21_out, and_1_out, and_2_out);
  and and_22 (and_22_out, and_3_out, and_4_out);
  and and_23 (and_23_out, and_5_out, and_6_out);
  and and_24 (and_24_out, and_7_out, and_8_out);
  and and_25 (and_25_out, and_9_out, and_10_out);
  and and_26 (and_26_out, and_11_out, and_12_out);
  and and_27 (and_27_out, and_13_out, and_14_out);
  and and_28 (and_28_out, and_15_out, and_16_out);
  and and_29 (and_29_out, and_17_out, and_18_out);
  and and_30 (and_30_out, and_19_out, and_20_out);
endmodule
