// Digital circuit 8BIT ALU A_S.dig as structural Verilog
module _8BIT_ALU_A_S (
  input  A1,
  input  B1,
  input  A2,
  input  B2,
  input  A3,
  input  B3,
  input  A4,
  input  B4,
  input  A5,
  input  B5,
  input  A6,
  input  B6,
  input  A7,
  input  B7,
  input  A8,
  input  B8,
  input  A_S,
  output C8,
  output S7,
  output S6,
  output S5,
  output S4,
  output S3,
  output S2,
  output S1,
  output S8
);

  wire FA1_c_o, FA2_c_o, FA3_c_o, FA4_c_o, FA5_c_o, FA6_c_o, FA7_c_o, xor_1_out, xor_2_out, xor_3_out,
       xor_4_out, xor_5_out, xor_6_out, xor_7_out, xor_8_out;

  Add FA8 (.a(A8), .b(xor_1_out), .c_i(FA7_c_o), .s(S8), .c_o(C8));
  xor xor_1 (xor_1_out, B8, A_S);
  xor xor_2 (xor_2_out, B7, A_S);
  Add FA7 (.a(A7), .b(xor_2_out), .c_i(FA6_c_o), .s(S7), .c_o(FA7_c_o));
  Add FA6 (.a(A6), .b(xor_3_out), .c_i(FA5_c_o), .s(S6), .c_o(FA6_c_o));
  xor xor_3 (xor_3_out, B6, A_S);
  xor xor_4 (xor_4_out, B5, A_S);
  Add FA5 (.a(A5), .b(xor_4_out), .c_i(FA4_c_o), .s(S5), .c_o(FA5_c_o));
  Add FA4 (.a(A4), .b(xor_5_out), .c_i(FA3_c_o), .s(S4), .c_o(FA4_c_o));
  xor xor_5 (xor_5_out, B4, A_S);
  xor xor_6 (xor_6_out, B3, A_S);
  Add FA3 (.a(A3), .b(xor_6_out), .c_i(FA2_c_o), .s(S3), .c_o(FA3_c_o));
  Add FA2 (.a(A2), .b(xor_7_out), .c_i(FA1_c_o), .s(S2), .c_o(FA2_c_o));
  xor xor_7 (xor_7_out, B2, A_S);
  xor xor_8 (xor_8_out, B1, A_S);
  Add FA1 (.a(A1), .b(xor_8_out), .c_i(A_S), .s(S1), .c_o(FA1_c_o));
endmodule
