// Digital circuit connecting ram with alu.dig as structural Verilog
module connecting_ram_with_alu (
  input  in_1,
  input  in_2,
  input  in_3,
  input  in_4,
  input  in_5,
  input  in_6,
  input  in_7,
  output out_8,
  output out_9,
  output out_10,
  output out_11
);

  wire and_1_out, and_2_out, and_3_out, and_4_out, and_5_out, and_6_out, and_7_out, and_8_out, and_9_out,
       and_10_out, and_11_out, and_12_out, and_13_out, and_14_out, and_15_out, and_16_out, and_17_out,
       and_18_out, and_19_out, and_20_out, and_21_out, and_22_out, and_23_out, and_24_out, d_ff_1_q,
       d_ff_2_q, d_ff_3_q, d_ff_4_q, d_ff_5_q, d_ff_6_q, d_ff_7_q, d_ff_8_q, d_ff_9_q, d_ff_10_q, d_ff_11_q,
       d_ff_12_q, d_ff_13_q, d_ff_14_q, d_ff_15_q, d_ff_16_q, not_1_out, not_2_out, not_3_out, not_4_out,
       or_1_out, or_2_out, or_3_out, or_4_out, or_5_out, or_6_out, or_7_out, or_8_out;

  not not_1 (not_1_out, in_2);
  not not_2 (not_2_out, in_1);
  not not_3 (not_3_out, in_1);
  not not_4 (not_4_out, in_2);
  and and_1 (and_1_out, not_1_out, not_2_out);
  and and_2 (and_2_out, in_2, not_3_out);
  and and_3 (and_3_out, not_4_out, in_1);
  and and_4 (and_4_out, in_2, in_1);
  and and_5 (and_5_out, in_7, and_1_out);
  and and_6 (and_6_out, in_7, and_2_out);
  and and_7 (and_7_out, in_7, and_3_out);
  and and_8 (and_8_out, in_7, and_4_out);
  D_FF d_ff_1 (.D(in_5), .C(and_5_out), .Q(d_ff_1_q));  // open: nQ
  D_FF d_ff_2 (.D(in_5), .C(and_6_out), .Q(d_ff_2_q));  // open: nQ
  D_FF d_ff_3 (.D(in_5), .C(and_7_out), .Q(d_ff_3_q));  // open: nQ
  D_FF d_ff_4 (.D(in_5), .C(and_8_out), .Q(d_ff_4_q));  // open: nQ
  D_FF d_ff_5 (.D(in_6), .C(and_5_out), .Q(d_ff_5_q));  // open: nQ
  D_FF d_ff_6 (.D(in_6), .C(and_6_out), .Q(d_ff_6_q));  // open: nQ
  D_FF d_ff_7 (.D(in_6), .C(and_7_out), .Q(d_ff_7_q));  // open: nQ
  D_FF d_ff_8 (.D(in_6), .C(and_8_out), .Q(d_ff_8_q));  // open: nQ
  D_FF d_ff_9 (.D(in_3), .C(and_5_out), .Q(d_ff_9_q));  // open: nQ
  D_FF d_ff_10 (.D(in_3), .C(and_6_out), .Q(d_ff_10_q));  // open: nQ
  D_FF d_ff_11 (.D(in_3), .C(and_7_out), .Q(d_ff_11_q));  // open: nQ
  D_FF d_ff_12 (.D(in_3), .C(and_8_out), .Q(d_ff_12_q));  // open: nQ
  D_FF d_ff_13 (.D(in_4), .C(and_5_out), .Q(d_ff_13_q));  // open: nQ
  and and_9 (and_9_out, d_ff_13_q, and_1_out);
  and and_10 (and_10_out, d_ff_9_q, and_1_out);
  and and_11 (and_11_out, d_ff_5_q, and_1_out);
  and and_12 (and_12_out, d_ff_1_q, and_1_out);
  D_FF d_ff_14 (.D(in_4), .C(and_6_out), .Q(d_ff_14_q));  // open: nQ
  and and_13 (and_13_out, d_ff_14_q, and_2_out);
  and and_14 (and_14_out, d_ff_10_q, and_2_out);
  and and_15 (and_15_out, d_ff_6_q, and_2_out);
  and and_16 (and_16_out, d_ff_2_q, and_2_out);
  D_FF d_ff_15 (.D(in_4), .C(and_7_out), .Q(d_ff_15_q));  // open: nQ
  and and_17 (and_17_out, d_ff_15_q, and_3_out);
  and and_18 (and_18_out, d_ff_11_q, and_3_out);
  and and_19 (and_19_out, d_ff_7_q, and_3_out);
  and and_20 (and_20_out, d_ff_3_q, and_3_out);
  D_FF d_ff_16 (.D(in_4), .C(and_8_out), .Q(d_ff_16_q));  // open: nQ
  and and_21 (and_21_out, d_ff_16_q, and_4_out);
  and and_22 (and_22_out, d_ff_12_q, and_4_out);
  and and_23 (and_23_out, d_ff_8_q, and_4_out);
  and and_24 (and_24_out, d_ff_4_q, and_4_out);
  or or_1 (or_1_out, and_12_out, and_16_out);
  or or_2 (or_2_out, and_20_out, and_24_out);
  or or_3 (or_3_out, and_11_out, and_15_out);
  or or_4 (or_4_out, and_19_out, and_23_out);
  or or_5 (or_5_out, and_10_out, and_14_out);
  or or_6 (or_6_out, and_18_out, and_22_out);
  or or_7 (or_7_out, and_9_out, and_13_out);
  or or_8 (or_8_out, and_17_out, and_21_out);
  or or_9 (out_11, or_1_out, or_2_out);
  or or_10 (out_10, or_3_out, or_4_out);
  or or_11 (out_9, or_5_out, or_6_out);
  or or_12 (out_8, or_7_out, or_8_out);
endmodule
