// Digital circuit full adder.dig as structural Verilog
module full_adder (
  input  A,
  input  B,
  input  A_2,
  input  B_2,
  input  C,
  output SUM,
  output CARRY,
  output SUM_2
);

  wire and_1_out, and_2_out, and_3_out, and_4_out, or_2_out, xor_1_out, xor_3_out;

  xor xor_1 (xor_1_out, A, B);
  and and_1 (and_1_out, A, B);
  xor xor_2 (SUM, xor_1_out, or_2_out);
  and and_2 (and_2_out, xor_1_out, or_2_out);
  or or_1 (CARRY, and_2_out, and_1_out);
  xor xor_3 (xor_3_out, A_2, B_2);
  and and_3 (and_3_out, A_2, B_2);
  and and_4 (and_4_out, xor_3_out, C);
  xor xor_4 (SUM_2, xor_3_out, C);
  or or_2 (or_2_out, and_4_out, and_3_out);
endmodule
